// Logisim project Project 7 Segment.circ as structural Verilog: 1 circuit, main circuit main
module main (
);

  wire clock_1_out, d_ff_1_q, not_1_out, xor_1_out;

  Clock clock_1 (.out(clock_1_out));
  xor xor_1 (xor_1_out, d_ff_1_q, 1'b1);
  D_Flip_Flop d_ff_1 (.clk(clock_1_out), .D(xor_1_out), .Q(d_ff_1_q));  // open: Qn, preset, en, reset
  not not_1 (not_1_out, d_ff_1_q);
  _7_Segment_Display u_7_segment_display_1 (
    .g(d_ff_1_q), .f(not_1_out), .a(1'b1), .b(d_ff_1_q), .e(not_1_out), .d(1'b1), .c(d_ff_1_q), .dp(1'b0));
  _7_Segment_Display u_7_segment_display_2 (
    .g(1'b1), .f(not_1_out), .a(1'b1), .b(d_ff_1_q), .e(1'b0), .d(1'b1), .c(1'b1), .dp(1'b0));
  _7_Segment_Display u_7_segment_display_3 (
    .g(not_1_out), .f(not_1_out), .a(not_1_out), .b(d_ff_1_q), .e(not_1_out), .d(not_1_out), .c(d_ff_1_q),
    .dp(1'b0));
endmodule
